# Fritzing sketch lyskryds-knap (saved by Fritzing 0.9.3b)
breadboards: 1

parts:
  Part1 = Arduino Uno (Rev3)
  LED1 = LED - 5mm [color="Green (555nm)" package="5 mm [THT]"]
  LED2 = LED - 5mm [color="Yellow (595nm)" package="5 mm [THT]"]
  LED3 = LED - 5mm [color="Red (633nm)" package="5 mm [THT]"]
  R1 = Resistor [tolerance=±5% resistance=220 package=THT]
  R2 = Resistor [tolerance=±5% resistance=220 package=THT]
  R3 = Resistor [tolerance=±5% resistance=220 package=THT]
  S1 = Pushbutton [package="[THT]"]
  R4 = Resistor [tolerance=±5% resistance=220 package=THT]

nets:
  N1: Part1.D11_PWM/MOSI, R1.Pin_1
  N2: Part1.D12/MISO, R2.Pin_1
  N3: Part1.D13/SCK, R3.Pin_1
  N4: Part1.D4, S1.Pin_3, S1.Pin_4, R4.Pin_1
  N5: Part1.5V, S1.Pin_1, S1.Pin_2
  N6: Part1.GND, LED1.cathode, LED2.cathode, LED3.cathode, R4.Pin_0
  N7: LED1.anode, R3.Pin_0
  N8: LED2.anode, R2.Pin_0
  N9: LED3.anode, R1.Pin_0
